# Fritzing sketch Smart Watering Plant Midterm (saved by Fritzing 1.0.2b)
breadboards: 1

parts:
  A1 = Particle - Photon2
  OLED_I2C1 = OLED 128x64 I2C Monochrome Display
  M1 = BMP280
  Breadboard5 = Breadboard Split Power
  Grove1 = Grove Dust Sensor
  Part1 = MQ-131 breakout
  Relay1 = Relay - 6 pins [package="DIP (Dual Inline) [THT]"]
  Incorrect_Moisture_Sensor_USE_one_with_AUOT_for_Analog_Pin = Chirp! Soil Moisture Sensor v2.7.3
  M2 = DC Motor [voltage_(max)=6V voltage_(min)=3V]
  R1 = Resistor [tolerance=±5% power=0.25W resistance=220 package=THT]
  Q1 = PNP-Transistor [package="TO92 [THT]"]
  R2 = Resistor [tolerance=±5% power=0.25W resistance=2200 package=THT]

nets:
  VCC: A1.Pin_2, A1.Pin_31, OLED_I2C1.VDD, Part1.VCC, Relay1.VCC, Incorrect_Moisture_Sensor_USE_one_with_AUOT_for_Analog_Pin.Pin_1
  GND: A1.Pin_4, A1.Pin_30, OLED_I2C1.GND, Breadboard5.pin3Z, Breadboard5.pin7Z, Breadboard5.pin26Z, Grove1.GND, Part1.GND, Relay1.GND, Incorrect_Moisture_Sensor_USE_one_with_AUOT_for_Analog_Pin.pin_5, M2.pin_1, Q1.C, R2.Pin_1
  N1: A1.Pin_5, Incorrect_Moisture_Sensor_USE_one_with_AUOT_for_Analog_Pin.pin_3
  N2: A1.Pin_7, Part1.AO
  N3: A1.Pin_17, OLED_I2C1.SCK, M1.SCL
  N4: A1.Pin_18, OLED_I2C1.SDA, M1.SDA
  N5: A1.Pin_20, Grove1.SIG
  N6: A1.Pin_26, Grove1.VCC, Relay1.ON, R1.Pin_0
  N7: Relay1.IN, R1.Pin_1, Q1.E
  N8: Relay1.COM, M2.pin_2
  N9: Q1.B, R2.Pin_0

custom parts:
  Particle - Photon2: The Photon 2 is a microcontroller and Wi-Fi networking developed by particle. Features: 802.11a/b/g/n Wi-Fi, 2.4 GHz and 5 GHz Integrated PCB antenna Integrated U.FL connector for external antenna Integrated RF switch BLE 5 using same antenna as Wi-Fi Realtek RTL8721DM MCU ARM Cortex M33 CPU, 200 MHz 2048 KB (2 MB) user application maximum size 3072 KB (3 MB) of RAM available to user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
  BMP280: Temperature Humidity Barometric presure Sensor, I2C
  Breadboard Split Power: A custom 6 pin per group power supply strip where the top row (ground) is all bussed together and the bottom row (+V) is split in two groups of 12 pins. This version is modified to be a loadable part and was rescaled to be on the standard 1px = 1thou grid with the size set in inches
  Grove Dust Sensor: PPD42 Grove Dust Sensor
  MQ-131 breakout: SKU: 101282
  Relay - 6 pins: A DIP stand-in part for whatever IC you want. With 6 pins on a 900mil dual inline package (DIP) footprint.
